# Fritzing sketch mputoy (saved by Fritzing 0.9.6b)
circuit board: 11.2606cm x 6.90311cm
breadboards: 2

parts:
  ESP32 = ESP32-38PinWide [part_number=ESP32-38PinWide]
  charger = SparkFun LiPo Charger Basic - Micro-USB [part_number=PRT-10217]
  S_UP = Pololu D24V5F3
  On/off = SPST Switch [package=switch-spdt_kit]
  C6 = Electrolytic Capacitor [capacitance=0.47mF voltage=35V package="100 mil [THT, electrolytic]"]
  D3 = Schottky Diode [part_number=1N5817 package="300 mil [THT]"]
  LED4 = LED - 3mm [color="Red (633nm)" current=0.030 package="3 mm [THT]"]
  R7 = Resistor [tolerance=±5% resistance=220 power=0.25 package=THT]
  LED5 = LED - 3mm [color="Red (633nm)" current=0.030 package="3 mm [THT]"]
  LED6 = LED - 3mm [color="Yellow (592nm)" current=0.030 package="3 mm [THT]"]
  R8 = Resistor [tolerance=±5% resistance=220 power=0.25 package=THT]
  R9 = Resistor [tolerance=±5% resistance=220 power=0.25 package=THT]
  MPU1 = InvenSense MPU6050
  DFRobot_DFPlayer_Mini2 = DFRobot DFPlayer Mini [part_number=DFR0299]
  C7 = Capacitor [package=cap-pth-small2]
  C8 = Capacitor [package=cap-pth-small2]
  SPKR = Loudspeaker
  Vol = Rotary Potentiometer (Small) [maximum_resistance=100kΩ package=THT]
  C9 = Capacitor [package=cap-pth-small2]
  R10 = Resistor [tolerance=±20% resistance=330 power=0.25 package=THT]
  strip1 = screw terminal, 3 pins
  C10 = Electrolytic Capacitor [capacitance=0.47mF voltage=35V package="100 mil [THT, electrolytic]"]

nets:
  N1: ESP32.3.3, Vol.leg2
  N2: ESP32.GPIO34, Vol.wiper
  N3: ESP32.GPIO32, R8.Pin_1
  N4: ESP32.GPIO25, R9.Pin_1
  GND: ESP32.GND, charger.GND, S_UP.GND, C6.-, LED4.cathode, LED5.cathode, LED6.cathode, MPU1.GND, DFRobot_DFPlayer_Mini2.GND-1, DFRobot_DFPlayer_Mini2.GND-2, C7.1, C8.1, Vol.leg1, C9.1, strip1.pin3, C10.-
  N5: ESP32.GPIO13, R10.Pin_0
  N6: ESP32.VIN, D3.cathode, C7.2
  N7: ESP32.GPIO16, DFRobot_DFPlayer_Mini2.TX
  N8: ESP32.GPIO17, DFRobot_DFPlayer_Mini2.RX
  N9: ESP32.GPIO21, MPU1.SDA
  N10: ESP32.GPIO22, MPU1.SCL
  N11: charger.VCC, On/off.P
  VCC: S_UP.VOUT, C6.+, D3.anode, R7.Pin_0, MPU1.VCC, DFRobot_DFPlayer_Mini2.VCC, C8.2, C9.2, strip1.pin1, C10.+
  N12: S_UP.VIN, On/off.O
  N13: LED4.anode, R7.Pin_1
  N14: LED5.anode, R9.Pin_0
  N15: LED6.anode, R8.Pin_0
  N16: DFRobot_DFPlayer_Mini2.SPK_1, SPKR.pin2
  N17: DFRobot_DFPlayer_Mini2.SPK_2, SPKR.pin1
  N18: R10.Pin_1, strip1.pin2

notes:
  3.7 lipo up to 5.2V (step up module) + switch on/off.
  https://techexplorations.com/guides/esp32/begin/power/
  it needs to be in 6-7 volts range(max 12V)
  This is a modified step down module, the real module is:
  step up pololu s7v8f5
  https://www.pololu.com/product/2123
  pin in this order: shdn vin gnd vout (pay attention in the schematic because the graphic is inverted) this is the real connection !!! shdn is not connected
  LED POWER
  LIPO CHARGER
  sparkfun
  https://www.sparkfun.com/products/10217
  Debug LEDs BT receiving (Airplane and car buttons on godot app) LED1 Y LED2 R
  R_led = 150/220 Ohm
  MPU 9250
  SDA G21; SCL G22
  ceramic decoupling 100 nF
  DIODE FOR DIVIDING USB AND LIPO SUPPLY: skotci diode byv1040 (minimal Voltage drop)
  STRIP LED 10 px : DO pin linked to G13 with 330 Ohm Resistor and a 470 uF capacitor on the supply
  potentiomenter 1 kOhm from the back: GND G34 3V3
  Volume Regulation
  DF PLAYER
  G16 (RX ESP) -> TX DF (3° starting from up and left)
  G17 (TX ESP) -> RX DF
  (2° starting from up and left)
  STRIP LED j1 CONNECTOR
  GND DO VIN
  100 nF capacitor decoupling esp32 supply (ceramic)
  470 uF decoupling power supply
  100 uF decoupling df player (ceramic)
  http://www.microcontroller.it/Tutorials/Elettronica/decuopling.htm
  Echo 1.0
  watch out for step up pins, they are not the one on the graphic, click on the pin for see the real name
  !!!!!!!!!!!!!!!!!!!!!!!!!!!!!!!!!!!!!!
  gnd
  vin
  vout
  Vcc
  ON
  OFF

custom parts:
  ESP32-38PinWide: Generic 38-Pin ESP32 with wide format (only access to one side of pins on a breadboard) based on Stephen Lilley's HiLetgo ESP-WROOM-32 ESP32 ESP-32S Development Board.
  SparkFun LiPo Charger Basic - Micro-USB: Description: If you need to charge LiPo batteries, this simple charger will do just that, and do it fast! The SparkFun LiPo Charger Basic is stripped down of all features and just does one thing well - charge 3.7V LiPo cells at a rate of 500mA. It is designed to charge single-cell Li-Ion or Li-Polymer batteries. Check the datasheet below to see if it will work with your battery. The board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
  Pololu D24V5F3: The compact (0.4″ × 0.5″) D24V5F3 synchronous buck voltage regulator takes an input voltage of up to 36 V and efficiently reduces it to 3.3 V while allowing for a maximum output current of 500 mA.
